// Logisim project mc_mcu.circ as structural Verilog
module main (
);

  wire CLK_out, cpu_1_csrwrt, cpu_1_mwrt, not_1_out, not_2_out, RST_out;
  wire [7:0] cpu_1_csro, cpu_1_maddr, cpu_1_mdato, ram_1_dout, ram_2_dout;
  wire [9:0] cpu_1_csraddr;
  wire [11:0] cpu_1_iaddr;
  wire [19:0] rom_1_data;

  Clock CLK (.out(CLK_out));
  Button RST (.out(RST_out));
  RAM #(.addrWidth(10), .asyncread("true")) ram_1 (
    .addr(cpu_1_csraddr), .we(cpu_1_csrwrt), .oe(not_1_out), .clk(CLK_out), .din(cpu_1_csro),
    .dout(ram_1_dout));
  not not_1 (not_1_out, cpu_1_csrwrt);
  CPU cpu_1 (
    .CLK(CLK_out), .RST(RST_out), .INSN(rom_1_data), .CSRI(ram_1_dout), .MDATI(ram_2_dout),
    .IADDR(cpu_1_iaddr), .CSRADDR(cpu_1_csraddr), .CSRWRT(cpu_1_csrwrt), .CSRO(cpu_1_csro),
    .MADDR(cpu_1_maddr), .MWRT(cpu_1_mwrt), .MDATO(cpu_1_mdato));
  RAM #(.asyncread("true")) ram_2 (
    .addr(cpu_1_maddr), .we(cpu_1_mwrt), .oe(not_2_out), .clk(CLK_out), .din(cpu_1_mdato), .dout(ram_2_dout));
  not not_2 (not_2_out, cpu_1_mwrt);
  ROM #(.addrWidth(12), .dataWidth(20)) rom_1 (.addr(cpu_1_iaddr), .data(rom_1_data));

  // Notes on the sheet:
  //   contents of rom_1 (hex, n*v repeats v):
  //   90010 0 1220 811ff e17fe 11*0 8010a 31180 2038a 20 3220 833ff e37fe f2c01 804cc 400a f4802 5b d001e
  //   91020 801f0 f0000
endmodule

module CU (
  input  [19:0] INSN,
  input  [7:0] RS_VAL,
  output JREG,
  output [1:0] NPC_MODE,
  output [3:0] RF_RI1,
  output [3:0] RF_RI2,
  output RF_WRT,
  output [3:0] RF_WI,
  output CPUSH,
  output CPOP,
  output OPUSH,
  output OPOP,
  output [3:0] ALU_FN,
  output M2RF,
  output MWRT,
  output I2ALU,
  output [11:0] IMM12_OUT,
  output CSR2RF,
  output CSRWRT
);

  wire ADD, ADDI, and_1_out, ANDI, BEQZ, BGTZ, BITMAN, BLTZ, BNEZ, BT1, BT2, BTYPE, CLR, CMPE, CMPG, CMPIE,
       CMPIG, CMPIL, CMPIN, CMPIU, CMPL, CMPN, CMPU, comparator_1_eq, comparator_1_gt, comparator_1_lt, JMP,
       LAND, LJMP, LOR, LXOR, multiplexer_3_out, not_2_out, not_3_out, or_1_out, ORI, RTYPE, SAR, SET, SHL,
       SHR, SUB, XORI;
  wire [1:0] multiplexer_1_out, multiplexer_2_out, multiplexer_6_out, multiplexer_9_out;
  wire [3:0] multiplexer_4_out, multiplexer_7_out, multiplexer_8_out, multiplexer_11_out, multiplexer_15_out;
  wire [3:3] not_1_out;
  wire [11:0] bit_extender_1_out, bit_extender_2_out, bit_extender_3_out, multiplexer_5_out,
       multiplexer_10_out;

  Decoder #(.enable("false"), .select(4)) decoder_1 (
    .out0(RTYPE), .out1(BITMAN), .out2(M2RF), .out3(MWRT), .out4(CMPIE), .out5(CMPIN), .out6(CMPIG),
    .out7(CMPIL), .out8(ADDI), .out9(LJMP), .out10(ANDI), .out11(ORI), .out12(XORI), .out13(CPUSH),
    .out14(BT1), .out15(BT2), .sel(INSN[19:16]));
  Decoder #(.select(4)) decoder_2 (
    .out0(ADD), .out1(SUB), .out2(LAND), .out3(LOR), .out4(LXOR), .out5(SAR), .out6(SHL), .out7(SHR),
    .out8(SET), .out9(CLR), .out10(OPUSH), .out11(OPOP), .out12(CMPE), .out13(CMPN), .out14(CMPG),
    .out15(CMPL), .sel(INSN[3:0]), .en(RTYPE));
  Multiplexer #(.width(2)) multiplexer_1 (.in0(2'b01), .in1(2'b11), .out(multiplexer_1_out), .sel(CPOP));
  not not_1 (not_1_out[3], INSN[19]);
  assign bit_extender_1_out = {{4{INSN[7]}}, INSN[7:0]};  // Bit_Extender bit_extender_1
  assign bit_extender_2_out = {{9{INSN[7]}}, INSN[7:5]};  // Bit_Extender bit_extender_2
  Decoder #(.select(2)) decoder_3 (.out0(BEQZ), .out1(BNEZ), .out2(BGTZ), .out3(BLTZ), .sel(INSN[11:10]), .en(BT1));
  Decoder #(.select(2)) decoder_4 (.out0(CPOP), .out1(JMP), .out2(CSR2RF), .out3(CSRWRT), .sel(INSN[11:10]), .en(BT2));
  Multiplexer #(.width(2)) multiplexer_2 (.in0(multiplexer_1_out), .in1(2'b00), .out(multiplexer_2_out), .sel(JMP));
  Comparator comparator_1 (.a(RS_VAL), .b({8{1'b0}}), .gt(comparator_1_gt), .eq(comparator_1_eq), .lt(comparator_1_lt));
  not not_2 (not_2_out, comparator_1_eq);
  Multiplexer #(.select(2)) multiplexer_3 (
    .in0(comparator_1_eq), .in1(not_2_out), .in2(comparator_1_gt), .in3(comparator_1_lt),
    .out(multiplexer_3_out), .sel(INSN[11:10]));
  or or_1 (or_1_out, MWRT, M2RF);
  Multiplexer #(.width(4)) multiplexer_4 (
    .in0({not_1_out[3], INSN[18:16]}), .in1(INSN[3:0]), .out(multiplexer_4_out), .sel(BITMAN));
  Multiplexer #(.width(12)) multiplexer_5 (
    .in0(bit_extender_1_out), .in1(bit_extender_2_out), .out(multiplexer_5_out), .sel(BITMAN));
  Multiplexer #(.width(2)) multiplexer_6 (.in0(2'b01), .in1(2'b00), .out(multiplexer_6_out), .sel(multiplexer_3_out));
  Multiplexer #(.width(4)) multiplexer_7 (
    .in0(multiplexer_4_out), .in1(4'b0000), .out(multiplexer_7_out), .sel(or_1_out));
  Multiplexer #(.width(4)) multiplexer_8 (
    .in0(4'b0000), .in1({INSN[11:10], 2'b11}), .out(multiplexer_8_out), .sel(BT1));
  Multiplexer #(.width(2)) multiplexer_9 (
    .in0(multiplexer_2_out), .in1(multiplexer_6_out), .out(multiplexer_9_out), .sel(BT1));
  Multiplexer #(.width(12)) multiplexer_10 (
    .in0(INSN[11:0]), .in1(multiplexer_5_out), .out(multiplexer_10_out), .sel(I2ALU));
  assign bit_extender_3_out = {{2{INSN[9]}}, INSN[9:0]};  // Bit_Extender bit_extender_3
  not not_3 (not_3_out, MWRT);
  Multiplexer #(.width(4)) multiplexer_11 (
    .in0(multiplexer_7_out), .in1(multiplexer_8_out), .out(multiplexer_11_out), .sel(BTYPE));
  Multiplexer #(.width(2)) multiplexer_12 (.in0(multiplexer_9_out), .in1(2'b10), .out(NPC_MODE), .sel(JREG));
  and and_1 (and_1_out, I2ALU, not_3_out);
  Multiplexer #(.width(12)) multiplexer_13 (
    .in0(multiplexer_10_out), .in1(bit_extender_3_out), .out(IMM12_OUT), .sel(BTYPE));
  or or_2 (CMPU, CMPE, CMPN, CMPG, CMPL);
  or or_3 (CMPIU, CMPIE, CMPIN, CMPIG, CMPIL);
  or or_4 (RF_WRT, RTYPE, and_1_out, CSR2RF);
  Multiplexer #(.width(4)) multiplexer_14 (.in0(multiplexer_11_out), .in1(INSN[3:0]), .out(ALU_FN), .sel(RTYPE));
  Multiplexer #(.width(4)) multiplexer_15 (.in0(INSN[15:12]), .in1(INSN[11:8]), .out(multiplexer_15_out), .sel(I2ALU));
  or or_5 (I2ALU, BITMAN, M2RF, MWRT, CMPIU, ADDI, ANDI, ORI, XORI);
  or or_6 (BTYPE, BT1, BT2);
  or or_7 (JREG, LJMP, CPUSH);
  Multiplexer #(.width(4)) multiplexer_16 (.in0(multiplexer_15_out), .in1(INSN[7:4]), .out(RF_WI), .sel(RTYPE));

  assign RF_RI1 = INSN[15:12];
  assign RF_RI2 = INSN[11:8];

  // Other names for the same wires on the sheet: OPC[3:0] = INSN[19:16]; BTFN[1:0] = INSN[11:10];
  //   IMM12[11:0] = INSN[11:0]; RT[3:0] = INSN[11:8]; ILOAD = M2RF; INCSR = CSR2RF; FUNC[3:0] = INSN[3:0];
  //   IMM8[7:0] = INSN[7:0]; IMM10[9:0] = INSN[9:0]; RD[3:0] = INSN[7:4]; IMM3[2:0] = INSN[7:5];
  //   RS[3:0] = INSN[15:12]; INVOKE = CPUSH; ISTORE = MWRT; ITYPE = I2ALU; JTYPE = JREG; OUTCSR = CSRWRT; POP = OPOP;
  //   PUSH = OPUSH; RET = CPOP
endmodule

module ALU (
  input  [3:0] FUNC,
  input  [7:0] A,
  input  [7:0] B,
  output [7:0] Z
);

  wire comparator_1_eq, comparator_1_gt, comparator_1_lt, not_3_out;
  wire [7:0] adder_1_out, and_1_out, and_2_out, bit_extender_1_out, bit_extender_2_out, bit_extender_3_out,
       bit_extender_4_out, multiplexer_1_out, not_1_out, not_2_out, or_1_out, or_2_out, shifter_1_out,
       shifter_2_out, shifter_3_out, shifter_4_out, xor_1_out;

  Multiplexer #(.width(8)) multiplexer_1 (.in0(B), .in1(not_1_out), .out(multiplexer_1_out), .sel(FUNC[0]));
  assign not_1_out = ~B;  // NOT_Gate not_1, 8 bits wide
  Shifter shifter_1 (.in(8'h1), .\dist (B[7:5]), .out(shifter_1_out));
  assign not_2_out = ~shifter_1_out;  // NOT_Gate not_2, 8 bits wide
  Comparator comparator_1 (.a(A), .b(B), .gt(comparator_1_gt), .eq(comparator_1_eq), .lt(comparator_1_lt));
  Adder adder_1 (.a(A), .b(multiplexer_1_out), .out(adder_1_out), .cin(FUNC[0]));  // open: cout
  assign and_1_out = A & B;  // AND_Gate and_1, 8 bits wide
  assign or_1_out = A | B;  // OR_Gate or_1, 8 bits wide
  assign xor_1_out = A ^ B;  // XOR_Gate xor_1, 8 bits wide
  Shifter #(.shift("ar")) shifter_2 (.in(A), .\dist (B[7:5]), .out(shifter_2_out));
  Shifter shifter_3 (.in(A), .\dist (B[7:5]), .out(shifter_3_out));
  Shifter #(.shift("lr")) shifter_4 (.in(A), .\dist (B[7:5]), .out(shifter_4_out));
  assign or_2_out = A | shifter_1_out;  // OR_Gate or_2, 8 bits wide
  assign and_2_out = A & not_2_out;  // AND_Gate and_2, 8 bits wide
  not not_3 (not_3_out, comparator_1_eq);
  assign bit_extender_1_out = {{7{1'b0}}, comparator_1_eq};  // Bit_Extender bit_extender_1
  assign bit_extender_2_out = {{7{1'b0}}, not_3_out};  // Bit_Extender bit_extender_2
  assign bit_extender_3_out = {{7{1'b0}}, comparator_1_gt};  // Bit_Extender bit_extender_3
  assign bit_extender_4_out = {{7{1'b0}}, comparator_1_lt};  // Bit_Extender bit_extender_4
  Multiplexer #(.select(4), .width(8)) multiplexer_2 (
    .in0(adder_1_out), .in1(adder_1_out), .in2(and_1_out), .in3(or_1_out), .in4(xor_1_out),
    .in5(shifter_2_out), .in6(shifter_3_out), .in7(shifter_4_out), .in8(or_2_out), .in9(and_2_out), .in10(A),
    .in11(A), .in12(bit_extender_1_out), .in13(bit_extender_2_out), .in14(bit_extender_3_out),
    .in15(bit_extender_4_out), .out(Z), .sel(FUNC));
endmodule

module NPC (
  input  [11:0] OFFSET,
  input  [1:0] MODE,
  input  [11:0] PREV_PC,
  input  [11:0] IMM_TARGET,
  output [11:0] NEXT_PC
);

  wire [11:0] multiplexer_1_out, multiplexer_2_out;

  Multiplexer #(.width(12)) multiplexer_1 (.in0(OFFSET), .in1(12'h1), .out(multiplexer_1_out), .sel(MODE[0]));
  Multiplexer #(.width(12)) multiplexer_2 (.in0(PREV_PC), .in1(IMM_TARGET), .out(multiplexer_2_out), .sel(MODE[1]));
  Adder #(.width(12)) adder_1 (.a(multiplexer_1_out), .b(multiplexer_2_out), .out(NEXT_PC), .cin(1'b0));  // open: cout
endmodule

module RF (
  input  [3:0] RI1,
  input  [3:0] RI2,
  input  WE,
  input  [3:0] WI,
  input  [7:0] WD,
  input  CLK,
  input  RST,
  output [7:0] RD1,
  output [7:0] RD2
);

  wire demultiplexer_1_out1, demultiplexer_1_out2, demultiplexer_1_out3, demultiplexer_1_out4,
       demultiplexer_1_out5, demultiplexer_1_out6, demultiplexer_1_out7, demultiplexer_1_out8,
       demultiplexer_1_out9, demultiplexer_1_out10, demultiplexer_1_out11, demultiplexer_1_out12,
       demultiplexer_1_out13, demultiplexer_1_out14, demultiplexer_1_out15;
  wire [7:0] register_1_q, register_2_q, register_3_q, register_4_q, register_5_q, register_6_q,
       register_7_q, register_8_q, register_9_q, register_10_q, register_11_q, register_12_q, register_13_q,
       register_14_q, register_15_q;

  Demultiplexer #(.select(4)) demultiplexer_1 (
    .out1(demultiplexer_1_out1), .out2(demultiplexer_1_out2), .out3(demultiplexer_1_out3),
    .out4(demultiplexer_1_out4), .out5(demultiplexer_1_out5), .out6(demultiplexer_1_out6),
    .out7(demultiplexer_1_out7), .out8(demultiplexer_1_out8), .out9(demultiplexer_1_out9),
    .out10(demultiplexer_1_out10), .out11(demultiplexer_1_out11), .out12(demultiplexer_1_out12),
    .out13(demultiplexer_1_out13), .out14(demultiplexer_1_out14), .out15(demultiplexer_1_out15), .in(WE),
    .sel(WI));  // open: out0
  Register register_1 (.D(WD), .en(demultiplexer_1_out4), .clk(CLK), .Q(register_1_q), .clr(RST));
  Register register_2 (.D(WD), .en(demultiplexer_1_out8), .clk(CLK), .Q(register_2_q), .clr(RST));
  Register register_3 (.D(WD), .en(demultiplexer_1_out12), .clk(CLK), .Q(register_3_q), .clr(RST));
  Register register_4 (.D(WD), .en(demultiplexer_1_out1), .clk(CLK), .Q(register_4_q), .clr(RST));
  Register register_5 (.D(WD), .en(demultiplexer_1_out5), .clk(CLK), .Q(register_5_q), .clr(RST));
  Register register_6 (.D(WD), .en(demultiplexer_1_out9), .clk(CLK), .Q(register_6_q), .clr(RST));
  Register register_7 (.D(WD), .en(demultiplexer_1_out13), .clk(CLK), .Q(register_7_q), .clr(RST));
  Register register_8 (.D(WD), .en(demultiplexer_1_out2), .clk(CLK), .Q(register_8_q), .clr(RST));
  Register register_9 (.D(WD), .en(demultiplexer_1_out6), .clk(CLK), .Q(register_9_q), .clr(RST));
  Register register_10 (.D(WD), .en(demultiplexer_1_out10), .clk(CLK), .Q(register_10_q), .clr(RST));
  Register register_11 (.D(WD), .en(demultiplexer_1_out14), .clk(CLK), .Q(register_11_q), .clr(RST));
  Register register_12 (.D(WD), .en(demultiplexer_1_out3), .clk(CLK), .Q(register_12_q), .clr(RST));
  Register register_13 (.D(WD), .en(demultiplexer_1_out7), .clk(CLK), .Q(register_13_q), .clr(RST));
  Register register_14 (.D(WD), .en(demultiplexer_1_out11), .clk(CLK), .Q(register_14_q), .clr(RST));
  Register register_15 (.D(WD), .en(demultiplexer_1_out15), .clk(CLK), .Q(register_15_q), .clr(RST));
  Multiplexer #(.select(4), .width(8)) multiplexer_1 (
    .in0({8{1'b0}}), .in1(register_4_q), .in2(register_8_q), .in3(register_12_q), .in4(register_1_q),
    .in5(register_5_q), .in6(register_9_q), .in7(register_13_q), .in8(register_2_q), .in9(register_6_q),
    .in10(register_10_q), .in11(register_14_q), .in12(register_3_q), .in13(register_7_q),
    .in14(register_11_q), .in15(register_15_q), .out(RD1), .sel(RI1));
  Multiplexer #(.select(4), .width(8)) multiplexer_2 (
    .in0({8{1'b0}}), .in1(register_4_q), .in2(register_8_q), .in3(register_12_q), .in4(register_1_q),
    .in5(register_5_q), .in6(register_9_q), .in7(register_13_q), .in8(register_2_q), .in9(register_6_q),
    .in10(register_10_q), .in11(register_14_q), .in12(register_3_q), .in13(register_7_q),
    .in14(register_11_q), .in15(register_15_q), .out(RD2), .sel(RI2));
endmodule

module STACK (
  input  CLK,
  input  RST,
  input  PUSH,
  input  POP,
  input  [7:0] DIN,
  output [7:0] DOUT
);

  wire and_3_out, and_4_out, and_5_out, and_6_out, and_7_out, and_8_out, and_9_out, and_10_out, or_2_out;
  wire [0:0] d_ff_1_q;
  wire [6:0] d_ff_8_q;
  wire [7:0] and_1_out, and_2_out, and_11_out, and_12_out, and_13_out, and_14_out, and_15_out, and_16_out,
       and_17_out, and_18_out, bit_extender_1_out, bit_extender_2_out, bit_extender_3_out,
       bit_extender_4_out, bit_extender_5_out, bit_extender_6_out, bit_extender_7_out, bit_extender_8_out,
       bit_extender_9_out, bit_extender_10_out, multiplexer_1_out, or_1_out, register_1_q, register_2_q,
       register_3_q, register_4_q, register_5_q, register_6_q, register_7_q, register_8_q;

  assign and_1_out = {d_ff_8_q, d_ff_1_q[0]} & bit_extender_1_out;  // AND_Gate and_1, 8 bits wide
  Multiplexer #(.width(8)) multiplexer_1 (
    .in0({d_ff_1_q[0], d_ff_8_q}), .in1(or_1_out), .out(multiplexer_1_out), .sel(or_2_out));
  assign or_1_out = and_1_out | and_2_out;  // OR_Gate or_1, 8 bits wide
  assign and_2_out = {d_ff_8_q[0], d_ff_1_q[0], d_ff_8_q[6:1]} & bit_extender_2_out;  // AND_Gate and_2, 8 bits wide
  assign bit_extender_1_out = {{7{POP}}, POP};  // Bit_Extender bit_extender_1
  assign bit_extender_2_out = {{7{PUSH}}, PUSH};  // Bit_Extender bit_extender_2
  D_Flip_Flop d_ff_1 (.D(multiplexer_1_out[7]), .clk(CLK), .Q(d_ff_1_q[0]), .reset(RST));  // open: Qn, preset
  D_Flip_Flop d_ff_2 (.D(multiplexer_1_out[6]), .clk(CLK), .Q(d_ff_8_q[6]), .reset(RST));  // open: Qn, preset
  D_Flip_Flop d_ff_3 (.D(multiplexer_1_out[5]), .clk(CLK), .Q(d_ff_8_q[5]), .reset(RST));  // open: Qn, preset
  D_Flip_Flop d_ff_4 (.D(multiplexer_1_out[4]), .clk(CLK), .Q(d_ff_8_q[4]), .reset(RST));  // open: Qn, preset
  D_Flip_Flop d_ff_5 (.D(multiplexer_1_out[3]), .clk(CLK), .Q(d_ff_8_q[3]), .reset(RST));  // open: Qn, preset
  D_Flip_Flop d_ff_6 (.D(multiplexer_1_out[2]), .clk(CLK), .Q(d_ff_8_q[2]), .reset(RST));  // open: Qn, preset
  D_Flip_Flop d_ff_7 (.D(multiplexer_1_out[1]), .clk(CLK), .Q(d_ff_8_q[1]), .reset(RST));  // open: Qn, preset
  D_Flip_Flop d_ff_8 (.D(multiplexer_1_out[0]), .clk(CLK), .Q(d_ff_8_q[0]), .preset(RST));  // open: Qn, reset
  or or_2 (or_2_out, PUSH, POP);
  Register register_1 (.D(DIN), .en(and_3_out), .clk(CLK), .Q(register_1_q), .clr(RST));
  and and_3 (and_3_out, PUSH, d_ff_8_q[0]);
  Register register_2 (.D(DIN), .en(and_4_out), .clk(CLK), .Q(register_2_q), .clr(RST));
  and and_4 (and_4_out, PUSH, d_ff_1_q[0]);
  Register register_3 (.D(DIN), .en(and_5_out), .clk(CLK), .Q(register_3_q), .clr(RST));
  and and_5 (and_5_out, PUSH, d_ff_8_q[6]);
  Register register_4 (.D(DIN), .en(and_6_out), .clk(CLK), .Q(register_4_q), .clr(RST));
  and and_6 (and_6_out, PUSH, d_ff_8_q[5]);
  Register register_5 (.D(DIN), .en(and_7_out), .clk(CLK), .Q(register_5_q), .clr(RST));
  and and_7 (and_7_out, PUSH, d_ff_8_q[4]);
  Register register_6 (.D(DIN), .en(and_8_out), .clk(CLK), .Q(register_6_q), .clr(RST));
  and and_8 (and_8_out, PUSH, d_ff_8_q[3]);
  Register register_7 (.D(DIN), .en(and_9_out), .clk(CLK), .Q(register_7_q), .clr(RST));
  and and_9 (and_9_out, PUSH, d_ff_8_q[2]);
  Register register_8 (.D(DIN), .en(and_10_out), .clk(CLK), .Q(register_8_q), .clr(RST));
  and and_10 (and_10_out, PUSH, d_ff_8_q[1]);
  assign bit_extender_3_out = {{7{d_ff_1_q[0]}}, d_ff_1_q[0]};  // Bit_Extender bit_extender_3
  assign bit_extender_4_out = {{7{d_ff_8_q[6]}}, d_ff_8_q[6]};  // Bit_Extender bit_extender_4
  assign bit_extender_5_out = {{7{d_ff_8_q[5]}}, d_ff_8_q[5]};  // Bit_Extender bit_extender_5
  assign bit_extender_6_out = {{7{d_ff_8_q[4]}}, d_ff_8_q[4]};  // Bit_Extender bit_extender_6
  assign bit_extender_7_out = {{7{d_ff_8_q[3]}}, d_ff_8_q[3]};  // Bit_Extender bit_extender_7
  assign bit_extender_8_out = {{7{d_ff_8_q[2]}}, d_ff_8_q[2]};  // Bit_Extender bit_extender_8
  assign bit_extender_9_out = {{7{d_ff_8_q[1]}}, d_ff_8_q[1]};  // Bit_Extender bit_extender_9
  assign bit_extender_10_out = {{7{d_ff_8_q[0]}}, d_ff_8_q[0]};  // Bit_Extender bit_extender_10
  assign and_11_out = register_1_q & bit_extender_3_out;  // AND_Gate and_11, 8 bits wide
  assign and_12_out = register_2_q & bit_extender_4_out;  // AND_Gate and_12, 8 bits wide
  assign and_13_out = register_3_q & bit_extender_5_out;  // AND_Gate and_13, 8 bits wide
  assign and_14_out = register_4_q & bit_extender_6_out;  // AND_Gate and_14, 8 bits wide
  assign and_15_out = register_5_q & bit_extender_7_out;  // AND_Gate and_15, 8 bits wide
  assign and_16_out = register_6_q & bit_extender_8_out;  // AND_Gate and_16, 8 bits wide
  assign and_17_out = register_7_q & bit_extender_9_out;  // AND_Gate and_17, 8 bits wide
  assign and_18_out = register_8_q & bit_extender_10_out;  // AND_Gate and_18, 8 bits wide
  assign DOUT = and_11_out | and_12_out | and_13_out | and_14_out | and_15_out | and_16_out | and_17_out | and_18_out;  // OR_Gate or_3, 8 bits wide
endmodule

module CSTACK (
  input  CLK,
  input  RST,
  input  PUSH,
  input  POP,
  input  [11:0] DIN,
  output [11:0] DOUT
);

  wire and_3_out, and_4_out, and_5_out, and_6_out, and_7_out, and_8_out, and_9_out, and_10_out, or_2_out;
  wire [0:0] d_ff_1_q;
  wire [6:0] d_ff_8_q;
  wire [7:0] and_1_out, and_2_out, bit_extender_1_out, bit_extender_2_out, multiplexer_1_out, or_1_out;
  wire [11:0] and_11_out, and_12_out, and_13_out, and_14_out, and_15_out, and_16_out, and_17_out, and_18_out,
       bit_extender_3_out, bit_extender_4_out, bit_extender_5_out, bit_extender_6_out, bit_extender_7_out,
       bit_extender_8_out, bit_extender_9_out, bit_extender_10_out, register_1_q, register_2_q, register_3_q,
       register_4_q, register_5_q, register_6_q, register_7_q, register_8_q;

  assign and_1_out = {d_ff_8_q, d_ff_1_q[0]} & bit_extender_1_out;  // AND_Gate and_1, 8 bits wide
  Multiplexer #(.width(8)) multiplexer_1 (
    .in0({d_ff_1_q[0], d_ff_8_q}), .in1(or_1_out), .out(multiplexer_1_out), .sel(or_2_out));
  assign or_1_out = and_1_out | and_2_out;  // OR_Gate or_1, 8 bits wide
  assign and_2_out = {d_ff_8_q[0], d_ff_1_q[0], d_ff_8_q[6:1]} & bit_extender_2_out;  // AND_Gate and_2, 8 bits wide
  assign bit_extender_1_out = {{7{POP}}, POP};  // Bit_Extender bit_extender_1
  assign bit_extender_2_out = {{7{PUSH}}, PUSH};  // Bit_Extender bit_extender_2
  D_Flip_Flop d_ff_1 (.D(multiplexer_1_out[7]), .clk(CLK), .Q(d_ff_1_q[0]), .reset(RST));  // open: Qn, preset
  D_Flip_Flop d_ff_2 (.D(multiplexer_1_out[6]), .clk(CLK), .Q(d_ff_8_q[6]), .reset(RST));  // open: Qn, preset
  D_Flip_Flop d_ff_3 (.D(multiplexer_1_out[5]), .clk(CLK), .Q(d_ff_8_q[5]), .reset(RST));  // open: Qn, preset
  D_Flip_Flop d_ff_4 (.D(multiplexer_1_out[4]), .clk(CLK), .Q(d_ff_8_q[4]), .reset(RST));  // open: Qn, preset
  D_Flip_Flop d_ff_5 (.D(multiplexer_1_out[3]), .clk(CLK), .Q(d_ff_8_q[3]), .reset(RST));  // open: Qn, preset
  D_Flip_Flop d_ff_6 (.D(multiplexer_1_out[2]), .clk(CLK), .Q(d_ff_8_q[2]), .reset(RST));  // open: Qn, preset
  D_Flip_Flop d_ff_7 (.D(multiplexer_1_out[1]), .clk(CLK), .Q(d_ff_8_q[1]), .reset(RST));  // open: Qn, preset
  D_Flip_Flop d_ff_8 (.D(multiplexer_1_out[0]), .clk(CLK), .Q(d_ff_8_q[0]), .preset(RST));  // open: Qn, reset
  or or_2 (or_2_out, PUSH, POP);
  Register #(.width(12)) register_1 (.D(DIN), .en(and_3_out), .clk(CLK), .Q(register_1_q), .clr(RST));
  and and_3 (and_3_out, PUSH, d_ff_8_q[0]);
  Register #(.width(12)) register_2 (.D(DIN), .en(and_4_out), .clk(CLK), .Q(register_2_q), .clr(RST));
  and and_4 (and_4_out, PUSH, d_ff_1_q[0]);
  Register #(.width(12)) register_3 (.D(DIN), .en(and_5_out), .clk(CLK), .Q(register_3_q), .clr(RST));
  and and_5 (and_5_out, PUSH, d_ff_8_q[6]);
  Register #(.width(12)) register_4 (.D(DIN), .en(and_6_out), .clk(CLK), .Q(register_4_q), .clr(RST));
  and and_6 (and_6_out, PUSH, d_ff_8_q[5]);
  Register #(.width(12)) register_5 (.D(DIN), .en(and_7_out), .clk(CLK), .Q(register_5_q), .clr(RST));
  and and_7 (and_7_out, PUSH, d_ff_8_q[4]);
  Register #(.width(12)) register_6 (.D(DIN), .en(and_8_out), .clk(CLK), .Q(register_6_q), .clr(RST));
  and and_8 (and_8_out, PUSH, d_ff_8_q[3]);
  Register #(.width(12)) register_7 (.D(DIN), .en(and_9_out), .clk(CLK), .Q(register_7_q), .clr(RST));
  and and_9 (and_9_out, PUSH, d_ff_8_q[2]);
  Register #(.width(12)) register_8 (.D(DIN), .en(and_10_out), .clk(CLK), .Q(register_8_q), .clr(RST));
  and and_10 (and_10_out, PUSH, d_ff_8_q[1]);
  assign bit_extender_3_out = {{11{d_ff_1_q[0]}}, d_ff_1_q[0]};  // Bit_Extender bit_extender_3
  assign bit_extender_4_out = {{11{d_ff_8_q[6]}}, d_ff_8_q[6]};  // Bit_Extender bit_extender_4
  assign bit_extender_5_out = {{11{d_ff_8_q[5]}}, d_ff_8_q[5]};  // Bit_Extender bit_extender_5
  assign bit_extender_6_out = {{11{d_ff_8_q[4]}}, d_ff_8_q[4]};  // Bit_Extender bit_extender_6
  assign bit_extender_7_out = {{11{d_ff_8_q[3]}}, d_ff_8_q[3]};  // Bit_Extender bit_extender_7
  assign bit_extender_8_out = {{11{d_ff_8_q[2]}}, d_ff_8_q[2]};  // Bit_Extender bit_extender_8
  assign bit_extender_9_out = {{11{d_ff_8_q[1]}}, d_ff_8_q[1]};  // Bit_Extender bit_extender_9
  assign bit_extender_10_out = {{11{d_ff_8_q[0]}}, d_ff_8_q[0]};  // Bit_Extender bit_extender_10
  assign and_11_out = register_1_q & bit_extender_3_out;  // AND_Gate and_11, 12 bits wide
  assign and_12_out = register_2_q & bit_extender_4_out;  // AND_Gate and_12, 12 bits wide
  assign and_13_out = register_3_q & bit_extender_5_out;  // AND_Gate and_13, 12 bits wide
  assign and_14_out = register_4_q & bit_extender_6_out;  // AND_Gate and_14, 12 bits wide
  assign and_15_out = register_5_q & bit_extender_7_out;  // AND_Gate and_15, 12 bits wide
  assign and_16_out = register_6_q & bit_extender_8_out;  // AND_Gate and_16, 12 bits wide
  assign and_17_out = register_7_q & bit_extender_9_out;  // AND_Gate and_17, 12 bits wide
  assign and_18_out = register_8_q & bit_extender_10_out;  // AND_Gate and_18, 12 bits wide
  assign DOUT = and_11_out | and_12_out | and_13_out | and_14_out | and_15_out | and_16_out | and_17_out | and_18_out;  // OR_Gate or_3, 12 bits wide
endmodule

module CPU (
  input  CLK,
  input  RST,
  input  [19:0] INSN,
  input  [7:0] CSRI,
  input  [7:0] MDATI,
  output [11:0] IADDR,
  output [9:0] CSRADDR,
  output CSRWRT,
  output [7:0] CSRO,
  output [7:0] MADDR,
  output MWRT,
  output [7:0] MDATO
);

  wire cu_1_cpop, cu_1_cpush, cu_1_csr2rf, cu_1_i2alu, cu_1_jreg, cu_1_m2rf, cu_1_opop, cu_1_opush,
       cu_1_rf_wrt;
  wire [1:0] cu_1_npc_mode;
  wire [3:0] cu_1_alu_fn, cu_1_rf_ri1, cu_1_rf_ri2, cu_1_rf_wi;
  wire [7:0] multiplexer_1_out, multiplexer_2_out, multiplexer_5_out, multiplexer_6_out, rf_1_rd2,
       stack_1_dout;
  wire [11:0] bit_extender_1_out, cstack_1_dout, multiplexer_3_out, multiplexer_4_out, npc_1_next_pc, PC_q;
  wire [11:10] cu_1_imm12_out;

  CU cu_1 (
    .INSN(INSN), .RS_VAL(CSRO), .JREG(cu_1_jreg), .NPC_MODE(cu_1_npc_mode), .RF_RI1(cu_1_rf_ri1),
    .RF_RI2(cu_1_rf_ri2), .RF_WRT(cu_1_rf_wrt), .RF_WI(cu_1_rf_wi), .CPUSH(cu_1_cpush), .CPOP(cu_1_cpop),
    .OPUSH(cu_1_opush), .OPOP(cu_1_opop), .ALU_FN(cu_1_alu_fn), .M2RF(cu_1_m2rf), .MWRT(MWRT),
    .I2ALU(cu_1_i2alu), .IMM12_OUT({cu_1_imm12_out, CSRADDR}), .CSR2RF(cu_1_csr2rf), .CSRWRT(CSRWRT));
  Multiplexer #(.width(8)) multiplexer_1 (
    .in0(multiplexer_2_out), .in1(CSRI), .out(multiplexer_1_out), .sel(cu_1_csr2rf));
  Multiplexer #(.width(8)) multiplexer_2 (
    .in0(multiplexer_6_out), .in1(MDATI), .out(multiplexer_2_out), .sel(cu_1_m2rf));
  CSTACK cstack_1 (.CLK(CLK), .RST(RST), .PUSH(cu_1_cpush), .POP(cu_1_cpop), .DIN(PC_q), .DOUT(cstack_1_dout));
  RF rf_1 (
    .RI1(cu_1_rf_ri1), .RI2(cu_1_rf_ri2), .WE(cu_1_rf_wrt), .WI(cu_1_rf_wi), .WD(multiplexer_1_out),
    .CLK(CLK), .RST(RST), .RD1(CSRO), .RD2(rf_1_rd2));
  assign bit_extender_1_out = {{4{CSRO[7]}}, CSRO};  // Bit_Extender bit_extender_1
  Multiplexer #(.width(12)) multiplexer_3 (
    .in0({cu_1_imm12_out, CSRADDR}), .in1(bit_extender_1_out), .out(multiplexer_3_out), .sel(cu_1_jreg));
  Multiplexer #(.width(12)) multiplexer_4 (
    .in0({cu_1_imm12_out, CSRADDR}), .in1(cstack_1_dout), .out(multiplexer_4_out), .sel(cu_1_cpop));
  Multiplexer #(.width(8)) multiplexer_5 (
    .in0(rf_1_rd2), .in1(CSRADDR[7:0]), .out(multiplexer_5_out), .sel(cu_1_i2alu));
  Multiplexer #(.width(8)) multiplexer_6 (.in0(MADDR), .in1(stack_1_dout), .out(multiplexer_6_out), .sel(cu_1_opop));
  Register #(.width(12)) PC (.D(npc_1_next_pc), .en(1'b1), .clk(CLK), .Q(PC_q), .clr(RST));
  NPC npc_1 (
    .OFFSET(multiplexer_3_out), .MODE(cu_1_npc_mode), .PREV_PC(PC_q), .IMM_TARGET(multiplexer_4_out),
    .NEXT_PC(npc_1_next_pc));
  ALU alu_1 (.FUNC(cu_1_alu_fn), .A(CSRO), .B(multiplexer_5_out), .Z(MADDR));
  STACK stack_1 (.CLK(CLK), .RST(RST), .PUSH(cu_1_opush), .POP(cu_1_opop), .DIN(CSRO), .DOUT(stack_1_dout));
  Multiplexer #(.width(12)) multiplexer_7 (.in0(PC_q), .in1({12{1'b0}}), .out(IADDR), .sel(RST));

  assign MDATO = CSRO;
endmodule

module CSR (
  input  [7:0] CSR_DATI,
  input  [9:0] ADDR,
  input  [9:0] CSR_ADDR,
  input  CSR_WRT,
  input  CLK,
  input  RST,
  output [7:0] CSR_DATO
);

  wire and_1_out, comparator_1_eq;

  Comparator #(.width(10)) comparator_1 (.a(ADDR), .b(CSR_ADDR), .eq(comparator_1_eq));  // open: gt, lt
  and and_1 (and_1_out, comparator_1_eq, CSR_WRT);
  Register register_1 (.D(CSR_DATI), .en(and_1_out), .clk(CLK), .Q(CSR_DATO), .clr(RST));
endmodule

module RSECC (
  input  CLK,
  input  [7:0] SDAT_IN,
  input  RST,
  input  ECC_ADDR,
  input  SDAT_IN_RDY,
  output RDY,
  output REQ_WORD,
  output [7:0] ECC_OUT
);

  wire not_1_out, X_p2, X_p14;
  wire [7:0] and_1_out, and_2_out, and_3_out, and_4_out, and_5_out, and_6_out, B0_q, B1_q,
       bit_extender_1_out, bit_extender_2_out, bit_extender_3_out, bit_extender_4_out, bit_extender_5_out,
       multiplexer_1_out, multiplexer_2_out, shifter_1_out, shifter_2_out, shifter_3_out, xor_1_out,
       xor_2_out, xor_3_out, xor_4_out, xor_5_out, xor_6_out, Z0_q, Z1_q;

  assign and_1_out = 8'h3 & bit_extender_5_out;  // AND_Gate and_1, 8 bits wide
  Multiplexer #(.width(8)) multiplexer_1 (.in0(and_1_out), .in1(xor_2_out), .out(multiplexer_1_out));  // open: sel
  Register Z0 (.D(multiplexer_1_out), .en(1'b1), .clk(CLK), .Q(Z0_q));  // open: clr
  Register B0 (.D(Z0_q), .en(1'b1), .clk(X_p2), .Q(B0_q), .clr(RST));
  Shifter #(.shift("lr")) shifter_1 (.in(Z0_q), .\dist (3'b001), .out(shifter_1_out));
  assign bit_extender_1_out = {{7{X_p14}}, X_p14};  // Bit_Extender bit_extender_1
  assign bit_extender_2_out = {{7{Z0_q[7]}}, Z0_q[7]};  // Bit_Extender bit_extender_2
  assign and_2_out = bit_extender_1_out & 8'h3;  // AND_Gate and_2, 8 bits wide
  assign and_3_out = bit_extender_2_out & 8'h1d;  // AND_Gate and_3, 8 bits wide
  assign xor_1_out = and_2_out ^ and_3_out;  // XOR_Gate xor_1, 8 bits wide
  assign xor_2_out = shifter_1_out ^ xor_1_out;  // XOR_Gate xor_2, 8 bits wide
  assign and_4_out = 8'h2 & bit_extender_5_out;  // AND_Gate and_4, 8 bits wide
  Multiplexer #(.width(8)) multiplexer_2 (.in0(and_4_out), .in1(xor_5_out), .out(multiplexer_2_out));  // open: sel
  Register Z1 (.D(multiplexer_2_out), .en(1'b1), .clk(CLK), .Q(Z1_q));  // open: clr
  Shifter #(.shift("lr")) shifter_2 (.in(Z1_q), .\dist (3'b001), .out(shifter_2_out));
  assign bit_extender_3_out = {{7{X_p14}}, X_p14};  // Bit_Extender bit_extender_3
  assign bit_extender_4_out = {{7{Z1_q[7]}}, Z1_q[7]};  // Bit_Extender bit_extender_4
  Register B1 (.D(xor_3_out), .en(1'b1), .clk(X_p2), .Q(B1_q), .clr(RST));
  assign xor_3_out = Z1_q ^ B0_q;  // XOR_Gate xor_3, 8 bits wide
  assign and_5_out = bit_extender_3_out & 8'h2;  // AND_Gate and_5, 8 bits wide
  assign and_6_out = bit_extender_4_out & 8'h1d;  // AND_Gate and_6, 8 bits wide
  assign xor_4_out = and_5_out ^ and_6_out;  // XOR_Gate xor_4, 8 bits wide
  assign xor_5_out = shifter_2_out ^ xor_4_out;  // XOR_Gate xor_5, 8 bits wide
  assign xor_6_out = SDAT_IN ^ B1_q;  // XOR_Gate xor_6, 8 bits wide
  assign bit_extender_5_out = {{7{xor_6_out[7]}}, xor_6_out[7]};  // Bit_Extender bit_extender_5
  not not_1 (not_1_out, X_p2);
  Shifter shifter_3 (.in(xor_6_out), .\dist (3'b001), .out(shifter_3_out));
  // Shift_Register X: pin names not known; wires that end beside it: RST, X_p2, not_1_out, CLK, 1'b0, shifter_3_out[0], shifter_3_out[1], shifter_3_out[2], shifter_3_out[3], shifter_3_out[4], shifter_3_out[5], shifter_3_out[6], shifter_3_out[7], X_p14
  Counter #(.max('h7), .width(3)) counter_1 (
    .load(1'b0), .up(1'b0), .count(1'b1), .clk(CLK), .carry(X_p2));  // open: clr, D, Q
  Counter #(.max('h7), .width(3)) counter_2 (.load(1'b0), .up(1'b0), .count(1'b1));  // open: clr, clk, D, carry, Q
endmodule
